// Logisim project 7segv2.circ as structural Verilog: 1 circuit, main circuit dec7segv2
module dec7segv2 (
  input  X3,
  input  X2,
  input  X1,
  input  X0,
  output a,
  output b,
  output c,
  output d,
  output e,
  output f,
  output g
);

  Multiplexer #(.select(4), .width(7), .enable("false")) multiplexer_1 (
    .in0(7'b0111111), .in1(7'b0000110), .in2(7'b1011011), .in3(7'b1001111), .in4(7'b1100110),
    .in5(7'b1101101), .in6(7'b1111101), .in7(7'b0000111), .in8({7{1'b1}}), .in9(7'b1101111),
    .in10(7'b1110111), .in11(7'b1111100), .in12(7'b0111001), .in13(7'b1011110), .in14(7'b1111001),
    .in15(7'b1110001), .out({g, f, e, d, c, b, a}), .sel({X3, X2, X1, X0}));

  // Notes on the sheet:
  //   Nom-prénom
  //   Nom-prénom
  //   Nom-prénom
  //   Nom-prénom
  //   L3Info-PFO
  //   L3Info-PFO
endmodule
