// Logisim project test7seg.circ as structural Verilog: 1 circuit, main circuit test7seg
module test7seg (
);

  wire dec7segv1_1_a, dec7segv1_1_b, dec7segv1_1_c, dec7segv1_1_d, dec7segv1_1_e, dec7segv1_1_f,
       dec7segv1_1_g, X_sw1, X_sw2, X_sw3, X_sw4;

  DipSwitch #(.number(4)) X (.sw1(X_sw1), .sw2(X_sw2), .sw3(X_sw3), .sw4(X_sw4));
  dec7segv1 dec7segv1_1 (
    .x3(X_sw1), .x2(X_sw2), .x1(X_sw3), .x0(X_sw4), .a(dec7segv1_1_a), .b(dec7segv1_1_b), .c(dec7segv1_1_c),
    .d(dec7segv1_1_d), .e(dec7segv1_1_e), .f(dec7segv1_1_f), .g(dec7segv1_1_g));
  _7_Segment_Display Y (
    .g(dec7segv1_1_g), .f(dec7segv1_1_f), .a(dec7segv1_1_a), .b(dec7segv1_1_b), .e(dec7segv1_1_e),
    .d(dec7segv1_1_d), .c(dec7segv1_1_c), .dp(1'b0));

  // Notes on the sheet:
  //   L3Info-PFO
  //   Nom-prénom
  //   Nom-prénom
endmodule
