// Logisim project BCD_WATCH.circ as structural Verilog: 1 circuit, main circuit Watch
module Watch (
  input  rst
);

  wire clk_out, MM_p6, SS_p6;
  wire [7:0] HH_p5, MM_p5, SS_p5;

  Clock clk (.out(clk_out));
  // DIGIT44_BCD SS: pin names not known; wires that end beside it: 8'h59, 1'b1, clk_out, rst, SS_p5, SS_p6
  // DIGIT44_BCD MM: pin names not known; wires that end beside it: 8'h59, SS_p6, clk_out, rst, MM_p5, MM_p6
  // DIGIT44_BCD HH: pin names not known; wires that end beside it: 8'h23, MM_p6, clk_out, rst, HH_p5
  // _7_Segment_Display H1: pin names not known; wires that end beside it: HH_p5[7:4], HH_p5[3:0]
  // BCD_to_7_Segment_decoder bcd_to_7_segment_decoder_1: pin names not known
  _7_Segment_Display H0 ();  // open: g, f, a, b, e, d, c, dp
  // BCD_to_7_Segment_decoder bcd_to_7_segment_decoder_2: pin names not known
  // BCD_to_7_Segment_decoder bcd_to_7_segment_decoder_3: pin names not known
  // _7_Segment_Display M1: pin names not known; wires that end beside it: MM_p5[7:4], MM_p5[3:0]
  _7_Segment_Display M0 ();  // open: g, f, a, b, e, d, c, dp
  // BCD_to_7_Segment_decoder bcd_to_7_segment_decoder_4: pin names not known
  // _7_Segment_Display S1: pin names not known; wires that end beside it: SS_p5[7:4], SS_p5[3:0]
  _7_Segment_Display S0 ();  // open: g, f, a, b, e, d, c, dp
  // BCD_to_7_Segment_decoder bcd_to_7_segment_decoder_5: pin names not known
  // BCD_to_7_Segment_decoder bcd_to_7_segment_decoder_6: pin names not known

  // Notes on the sheet:
  //   TP2 montre numérique 
endmodule
