// Logisim project DIGIT44_BCD.circ as structural Verilog: 2 circuits, main circuit DIGIT44_BCD
module DIGIT44_BCD (
  input  [7:0] P,
  input  inc,
  input  clk,
  input  rst,
  output tick,
  output [7:0] Q
);

  wire cpt4bcd_1_tick, cpt4bcd_2_tick;
  wire [3:0] cpt4bcd_1_q;
  wire [7:0] adder_1_out, multiplexer_1_out, register_1_q, subtractor_1_out;

  Adder adder_1 (.a(Q), .b(8'h1), .out(adder_1_out));  // open: cin, cout
  Multiplexer #(.width(8), .enable("false")) multiplexer_1 (
    .in0(adder_1_out), .in1({8{1'b0}}), .out(multiplexer_1_out), .sel(tick));
  Register register_1 (.D(multiplexer_1_out), .en(inc), .clk(clk), .Q(register_1_q), .clr(rst));
  Subtractor subtractor_1 (.a(P), .b(8'h1), .out(subtractor_1_out));  // open: bin, bout
  Comparator comparator_1 (.a(Q), .b(subtractor_1_out), .eq(tick));  // open: gt, lt
  CPT4BCD cpt4bcd_1 (
    .D(register_1_q[3:0]), .load(1'b1), .inc(1'b0), .clk(clk), .rst(rst), .Q(cpt4bcd_1_q),
    .Tick(cpt4bcd_1_tick));
  CPT4BCD cpt4bcd_2 (
    .D(register_1_q[7:4]), .load(1'b0), .inc(cpt4bcd_1_tick), .clk(clk), .rst(rst), .Q(Q[7:4]),
    .Tick(cpt4bcd_2_tick));
  Multiplexer #(.width(4), .enable("false")) multiplexer_2 (
    .in0(cpt4bcd_1_q), .in1(4'b0000), .out(Q[3:0]), .sel(cpt4bcd_1_tick));
endmodule

module test_DIGIT44_BCD (
  input  [7:0] P,
  input  inc,
  input  rst,
  output [7:0] Q,
  output tick
);

  wire clk_out, sysclk_out;

  Clock clk (.out(clk_out));
  Clock sysclk (.out(sysclk_out));
  DIGIT44_BCD digit44_bcd_1 (.P(P), .inc(inc), .clk(clk_out), .rst(rst), .tick(tick), .Q(Q));
endmodule
