// Logisim project TP3.circ as structural Verilog: 2 circuits, main circuit SREG8
module SREG8 (
  input  clk,
  input  rst,
  input  sin,
  input  [1:0] C,
  input  [7:0] D,
  output sout,
  output [7:0] Q
);

  wire xor_1_out;
  wire [7:0] multiplexer_1_out;

  Multiplexer #(.width(8), .enable("false")) multiplexer_1 (
    .in0({sin, Q[7:1]}), .in1(D), .out(multiplexer_1_out), .sel(C[0]));
  Register register_1 (.D(multiplexer_1_out), .en(xor_1_out), .clk(clk), .Q(Q), .clr(rst));
  xor xor_1 (xor_1_out, C[0], C[1]);

  assign sout = Q[0];
endmodule

module TP3_student (
  input  rst,
  output out_2
);

  wire clk, comparator_1_gt, comparator_1_lt, even_parity_1_out, fsm_entity_1_p5, fsm_entity_1_p6,
       fsm_entity_1_p7, mysterymessage_1_p3, or_1_out, sreg8_1_sout;
  wire [1:0] fsm_entity_1_p8;
  wire [7:0] sreg8_1_q;

  Clock sysclk (.out(clk));
  // MysteryMessage mysterymessage_1: pin names not known; wires that end beside it: clk, rst, mysterymessage_1_p3
  // FSM_Entity #(.content("state_machine example @[50,50,1000,600]{\n	in TX[1]   @[50,100,21,15];\n	out ACQ[1]   @[1018,140,32,15];REQ[1]   @[1018,188,32,15];Error[1]   @[1016,236,34,15];C[2]   @[1011,270,39,15];\n	codeWidth = 4;\n	reset = S0;\n	\n	state S0[\"0000\"]:\n	 	@[192,110,30,30]\n		set ACQ=\"0\";REQ=\"0\";Error=\"0\";C=\"00\";  @[192,110,30,30]	\n		goto S1  when (/TX)   @[289,134,33,21]; \n	state S1[\"0001\"]:\n	 	@[377,127,30,30]\n		set ACQ=\"0\";REQ=\"0\";Error=\"0\";C=\"10\";  @[377,127,30,30]	\n		goto S2  when default   @[458,151,43,21]; \n	state S2[\"0010\"]:\n	 	@[535,136,30,30]\n		set ACQ=\"0\";REQ=\"0\";Error=\"0\";C=\"10\";  @[535,136,30,30]	\n		goto S3  when default   @[635,157,43,21]; \n	state S3[\"0011\"]:\n	 	@[728,159,30,30]\n		set ACQ=\"0\";REQ=\"0\";Error=\"0\";C=\"10\";  @[728,159,30,30]	\n		goto S4  when default   @[782,219,43,21]; \n	state S4[\"0100\"]:\n	 	@[806,266,30,30]\n		set ACQ=\"0\";REQ=\"0\";Error=\"0\";C=\"10\";  @[806,266,30,30]	\n		goto S5  when default   @[863,323,43,21]; \n	state S5[\"0101\"]:\n	 	@[900,368,30,30]\n		set ACQ=\"0\";REQ=\"0\";Error=\"0\";C=\"10\";  @[900,368,30,30]	\n		goto S6  when default   @[905,449,43,21]; \n	state S6[\"0110\"]:\n	 	@[892,500,30,30]\n		set ACQ=\"0\";REQ=\"0\";Error=\"0\";C=\"10\";  @[892,500,30,30]	\n		goto S7  when default   @[808,538,43,21]; \n	state S7[\"0111\"]:\n	 	@[695,550,30,30]\n		set ACQ=\"0\";REQ=\"0\";Error=\"0\";C=\"10\";  @[695,550,30,30]	\n		goto S8  when default   @[598,570,43,21]; \n	state S8[\"1000\"]:\n	 	@[447,585,30,30]\n		set ACQ=\"0\";REQ=\"0\";Error=\"0\";C=\"10\";  @[447,585,30,30]	\n		goto S9  when default   @[306,603,43,21]; \n	state S9[\"1001\"]:\n	 	@[183,535,30,30]\n		set ACQ=\"0\";REQ=\"0\";Error=\"0\";C=\"00\";  @[183,535,30,30]	\n		goto S10_parity  when default   @[116,532,43,21]; \n	state S10_parity[\"1010\"]:\n	 	@[93,426,30,30]\n		set ACQ=\"0\";REQ=\"1\";Error=\"1\";C=\"00\";  @[93,426,30,30]	\n		goto S11  when default   @[90,368,43,21]; \n	state S11[\"1011\"]:\n	 	@[116,259,30,30]\n		set ACQ=\"1\";REQ=\"0\";Error=\"0\";C=\"00\";  @[116,259,30,30]	\n		goto S0  when TX   @[134,199,21,21]; \n}")) fsm_entity_1: pin names not known; wires that end beside it: clk, rst, 1'b1, mysterymessage_1_p3, fsm_entity_1_p5, fsm_entity_1_p6, fsm_entity_1_p7, fsm_entity_1_p8
  SREG8 sreg8_1 (
    .clk(clk), .rst(rst), .sin(mysterymessage_1_p3), .C(fsm_entity_1_p8), .D({8{1'b1}}), .sout(sreg8_1_sout),
    .Q(sreg8_1_q));
  // TTYPFO #(.cols(40)) ttypfo_1: pin names not known; wires that end beside it: clk, fsm_entity_1_p6, fsm_entity_1_p5, sreg8_1_q, rst
  // Probe on sreg8_1_q
  xnor even_parity_1 (even_parity_1_out, sreg8_1_q[0], sreg8_1_q[1], sreg8_1_q[2], sreg8_1_q[3], sreg8_1_q[4], sreg8_1_q[5], sreg8_1_q[6], sreg8_1_q[7]);
  Comparator #(.width(1)) comparator_1 (
    .a(sreg8_1_sout), .b(even_parity_1_out), .gt(comparator_1_gt), .lt(comparator_1_lt));  // open: eq
  or or_1 (or_1_out, comparator_1_gt, comparator_1_lt);
  and and_1 (out_2, or_1_out, fsm_entity_1_p7);

  // Notes on the sheet:
  //   Simulation de l'emetteur
  //   TX
  //   REQ
  //   ACK
  //   DATA
  //   Afficheur de caractères (code ASCII)
endmodule
